# Fritzing sketch Gree-up_electronic (saved by Fritzing 0.8.7b)
breadboards: 1

parts:
  Componente1 = Arduino Uno (Rev3)
  LED1 = LED - 5mm [color="Red (635nm)" package="5 mm [THT]"]
  LED2 = LED - 5mm [color="Green (565nm)" package="5 mm [THT]"]
  LED3 = LED - 5mm [color="Blue (430nm)" package="5 mm [THT]"]
  R1 = Photocell (LDR) [package=THT]
  LCD1 = LCD screen
  LCM1602_IIC5 = LCM1602 IIC [part_number="LCM1602 IIC" chip_label="LCM1602 IIC" package="DIP (Dual Inline) [THT]"]
  R2 = Resistor [tolerance=±5% resistance=220 package=THT]
  DHT4 = DHT11 Humitidy and Temperature Sensor
  R3 = Resistor [tolerance=±5% resistance=5k package=THT]
  U1 = G3VM-61E1 [package=g3vm-61e1]
  VCC1 = Battery block 9V
  M1 = DC Motor
  R4 = Resistor [tolerance=±5% resistance=220 package=THT]
  J1 = Peltier Element
  U2 = G3VM-61E1 [package=g3vm-61e1]
  VCC2 = Battery block 9V

nets:
  N1: Componente1.A0, R1.pin_0, R4.Pin_1
  N2: Componente1.A4/SDA, LCM1602_IIC5.SDA
  N3: Componente1.A5/SCL, LCM1602_IIC5.SCL
  N4: Componente1.D8, U2.P$2
  N5: Componente1.D2, LED1.anode
  N6: Componente1.D4, LED3.anode
  N7: Componente1.D5_PWM, LED2.anode
  N8: Componente1.D6_PWM, U1.P$2
  N9: Componente1.D7, DHT4.DATA, R3.Pin_0
  5V: Componente1.5V, R1.pin_1, LCM1602_IIC5.VCC, DHT4.VDD, R3.Pin_1, U1.P$3, U2.P$1, U2.P$3
  GND: Componente1.GND, LCM1602_IIC5.GND, R2.Pin_1, DHT4.GND, U1.P$1, R4.Pin_0
  N10: LED1.cathode, LED2.cathode, LED3.cathode, R2.Pin_0
  VSS: LCD1.VSS, LCM1602_IIC5.VSS
  VDD: LCD1.VDD, LCM1602_IIC5.VDD
  N11: LCD1.V0, LCM1602_IIC5.V0
  N12: LCD1.RS, LCM1602_IIC5.RS
  N13: LCD1.R/W, LCM1602_IIC5.RW
  N14: LCD1.E, LCM1602_IIC5.E
  N15: LCD1.DB0, LCM1602_IIC5.D0
  N16: LCD1.DB1, LCM1602_IIC5.D1
  N17: LCD1.DB2, LCM1602_IIC5.D2
  N18: LCD1.DB3, LCM1602_IIC5.D3
  N19: LCD1.DB4, LCM1602_IIC5.D4
  N20: LCD1.DB5, LCM1602_IIC5.D5
  N21: LCD1.DB6, LCM1602_IIC5.D6
  N22: LCD1.DB7, LCM1602_IIC5.D7
  N23: LCD1.LED+, LCM1602_IIC5.A
  N24: LCD1.LED-, LCM1602_IIC5.K
  N25: LCM1602_IIC5.LED_A, LCM1602_IIC5.LED_B
  N26: U1.P$4, VCC1.+
  N27: U1.P$6, M1.pin_1
  N28: J1.pin2, U2.P$4
  N29: U2.P$6, VCC2.+

notes:
  COLD generator
  SENSOR
  Temperature
  Humidity
  led lights
  12V
  (Battery)
  12V
  (Battery from the SOLAR PANEL)
  Electro mechanical
  lcd display

custom parts:
  LCM1602 IIC: I2C-Module to use a 1602 or 2004 LCD on with the wire.h libory Serial LCD Modul
  DHT11 Humitidy and Temperature Sensor: DHT11 Humidity and Temperature Sensor
