# Fritzing sketch watch (saved by Fritzing 0.8.7b)
breadboards: 1

parts:
  Parte1 = Arduino Mega 2560 (Rev3)
  U1 = LCD-16X2 [package=lcd-16x2]
  R1 = Rotary Potentiometer (Small) [maximum_resistance=100kΩ package=THT]
  Matrix_keypad1 = KEYPAD 4x4

nets:
  N1: Parte1.D13_PWM, U1.RS
  N2: Parte1.D12_PWM, U1.E
  N3: Parte1.D11_PWM, U1.DB4
  N4: Parte1.D10_PWM, U1.DB5
  N5: Parte1.D9_PWM, U1.DB6
  N6: Parte1.D8_PWM, U1.DB7
  5V: Parte1.5V, U1.VDD, U1.A, R1.leg2
  GND: Parte1.GND, U1.VSS, U1.R_W, U1.K, R1.leg1
  N7: Parte1.D0_RX0, Matrix_keypad1.col1
  N8: Parte1.D1_TX0, Matrix_keypad1.col2
  N9: Parte1.D2_PWM, Matrix_keypad1.col3
  N10: Parte1.D3_PWM, Matrix_keypad1.col4
  N11: Parte1.D4_PWM, Matrix_keypad1.row1
  N12: Parte1.D5_PWM, Matrix_keypad1.row2
  N13: Parte1.D6_PWM, Matrix_keypad1.row3
  N14: Parte1.D7_PWM, Matrix_keypad1.row4
  N15: U1.VO, R1.wiper

notes:
  Relog to control planting time

custom parts:
  KEYPAD 4x4: Matrix keypad 16 buttons, 4 rows x 4 columns

// code stored in the sketch: LCD_y_teclado4x4_fritzing.ino
#include <LiquidCrystal.h>
#include <Keypad.h>

LiquidCrystal lcd(13, 12, 11, 10, 9, 8);
unsigned long tiempoPas=0;
int pinAccion=14;
int pinEstado= LOW;
int numero=0;
int lapso=0;
int fotos=0;
//Config del Teclado
const byte filas=4;
const byte colum=4;

char botones[filas][colum]={
  {'1','2','3','A'},
  {'4','5','6','B'},
  {'7','8','9','C'},
  {'*','0','#','D'}
};

byte pinesFila[filas]={0,1,2,3};
byte pinesColu[colum]={4,5,6,7};
Keypad teclado=Keypad( makeKeymap(botones),pinesFila,pinesColu,filas,colum );
// ----------------------------

int numTeclado()
{
   int num = 0;
   char key = teclado.getKey();
   while(key != '#')
   {
      switch (key)
      {
         case NO_KEY:
            break;
         case '0': case '1': case '2': case '3': case '4':
         case '5': case '6': case '7': case '8': case '9':
            lcd.print(key);
            num = num * 10 + (key - '0');
            break;
         case '*':
            num = 0;
            lcd.clear();
            break;
      }
      key = teclado.getKey();
   }
   return num;
}


void setup(){
  lcd.begin(16,2);
  pinMode(pinAccion, OUTPUT);
}
  
  
void loop(){
  unsigned long tiempo=millis();
  
  if(numero==0){
      lcd.setCursor(0,0);
      lcd.print("Lapso:");
      lcd.setCursor(0,1);
      numero=numTeclado();
      lapso=long(numero)*1000;
      lcd.print("entro if");
  }
  else{
      if(tiempo - tiempoPas > lapso) {
        tiempoPas = tiempo;
        fotos=fotos+1;   
        pinEstado = HIGH;
        digitalWrite(pinAccion, pinEstado);
        delay(100);
        pinEstado = LOW;
        digitalWrite(pinAccion, pinEstado);
        lcd.clear();
        lcd.setCursor(0,0);
        lcd.print("Ejecutando");
        lcd.setCursor(0,1);
        String numFoto="Foto: " + String(fotos);
        lcd.print(numFoto);

      }
  }
}

// code stored in the sketch: reloj_simple_LCD_fritzing.ino
#include <Keypad.h>
#include <LiquidCrystal.h>

LiquidCrystal lcd(13, 12, 11, 10, 9, 8);

int h, m ,s =0;
unsigned long tiempoPas=0;
int segundo=1000;
boolean listo=false;

//Config del Teclado
const byte filas=4;
const byte colum=4;

char botones[filas][colum]={
  {
    '1','2','3','A'  }
  ,
  {
    '4','5','6','B'  }
  ,
  {
    '7','8','9','C'  }
  ,
  {
    '*','0','#','D'  }
};

byte pinesFila[filas]={
  0,1,2,3};
byte pinesColu[colum]={
  4,5,6,7};
Keypad teclado=Keypad( makeKeymap(botones),pinesFila,pinesColu,filas,colum );
// ----------------------------

int numTeclado()
{
  int num = 0;
  char key = teclado.getKey();
  while(key != '#')
  {
    switch (key)
    {
    case NO_KEY:
      break;
    case '0': 
    case '1': 
    case '2': 
    case '3': 
    case '4':
    case '5': 
    case '6': 
    case '7': 
    case '8': 
    case '9':
      lcd.print(key);
      num = num * 10 + (key - '0');
      break;
    case '*':
      num = 0;
      lcd.clear();
      break;
    }
    key = teclado.getKey();
  }
  return num;
}


void reloj(){
  s++;
  if(s>59){
    s=0;
    m++;
    if(m>59){
      m=0;
      h++;
      if(h<23){
        h=0;
      }
    }
  }
}

String formato(int num){
  String resultado="";
  if(num<10)
    resultado="0"+String(num);
  else
    resultado=String(num);
  return resultado;
}

void configurar(){
  lcd.setCursor(0,0);
  lcd.print("Hora:");
  lcd.setCursor(0,1);
  h=numTeclado();
  lcd.clear();

  lcd.setCursor(0,0);
  lcd.print("Minutos:");
  lcd.setCursor(0,1);
  m=numTeclado();
  lcd.clear();
  listo=true;
}


void setup() {
  lcd.begin(16,2);
}

void loop(){
  unsigned long tiempo=millis();
  if(listo){
    if(tiempo - tiempoPas > segundo) {
      tiempoPas = tiempo;
      reloj();
    }
    String laHora = "--- "+formato(h)+":"+formato(m)+":"+formato(s)+" ---";
    lcd.setCursor(0,0);
    lcd.print(laHora);
  }
  else{
    configurar();
  }
}
